// Logisim project as1-task1-1.circ as structural Verilog: 1 circuit, main circuit main
module main (
);

  wire and_1_out, and_2_out, and_3_out, and_4_out, button_1_out, button_2_out, not_1_out, not_2_out,
       undriven, undriven_2;

  Button button_1 (.out(button_1_out));
  not not_1 (not_1_out, button_1_out);
  Button button_2 (.out(button_2_out));
  not not_2 (not_2_out, button_2_out);
  and and_1 (and_1_out, undriven, undriven_2);
  and and_2 (and_2_out, undriven, not_2_out);
  and and_3 (and_3_out, undriven_2, not_1_out);
  and and_4 (and_4_out, not_2_out, not_1_out);

  // Notes on the sheet:
  //   A1
  //   A0
  //   Y3
  //   Y2
  //   Y1
  //   Y0
endmodule
