// Logisim project task3-1.circ as structural Verilog: 1 circuit, main circuit main
module main (
  input  Cin,
  input  [3:0] A,
  input  [3:0] B,
  input  Cout,
  output [3:0] S
);

  Adder #(.width(4)) adder_1 (.a(A), .b(B), .out(S), .cin(Cin), .cout(Cout));
endmodule
