// Logisim project task5-1.circ as structural Verilog: 2 circuits, main circuit main
module main (
  input  CLK,
  input  Din,
  output Q
);

  wire d_latch_1_q, not_1_out;

  d_latch d_latch_1 (.CLK(not_1_out), .D(Din), .Q(d_latch_1_q));  // open: Q_prime
  not not_1 (not_1_out, CLK);
  d_latch d_latch_2 (.CLK(CLK), .D(d_latch_1_q), .Q(Q));  // open: Q_prime

  // Notes on the sheet:
  //   master
  //   slave
endmodule

module d_latch (
  input  CLK,
  input  D,
  output Q,
  output Q_prime
);

  wire and_1_out, and_2_out, not_1_out;

  not not_1 (not_1_out, D);
  and and_1 (and_1_out, CLK, not_1_out);
  and and_2 (and_2_out, CLK, D);
  nor nor_1 (Q, and_1_out, Q_prime);
  nor nor_2 (Q_prime, Q, and_2_out);

  // Notes on the sheet:
  //   R
  //   S
endmodule
