// Logisim project task6-1.circ as structural Verilog: 1 circuit, main circuit main
module main (
  input  [7:0] in_1,
  input  E,
  input  pin,
  output [7:0] O
);

  wire button_1_out, clock_1_out;
  wire [7:0] adder_1_out, multiplexer_1_out, not_1_out;

  Button button_1 (.out(button_1_out));
  assign not_1_out = ~in_1;  // NOT_Gate not_1, 8 bits wide
  Multiplexer #(.width(8), .enable("false")) multiplexer_1 (
    .in0(in_1), .in1(not_1_out), .out(multiplexer_1_out), .sel(button_1_out));
  Adder adder_1 (.a(multiplexer_1_out), .b(O), .out(adder_1_out), .cin(button_1_out));  // open: cout
  Clock clock_1 (.out(clock_1_out));
  Register register_1 (.D(adder_1_out), .en(E), .Q(O), .clk(clock_1_out), .clr(pin));

  // Notes on the sheet:
  //   CLK
endmodule
